// Logisim project CPU2.circ as structural Verilog: 13 circuits, main circuit main
module main (
  input  in_1,
  input  in_2,
  input  in_3,
  input  in_4,
  input  in_5,
  input  in_6,
  input  in_7,
  input  in_8,
  input  in_9,
  input  Input,
  input  Output,
  input  in_12,
  input  Enable,
  input  Subtract,
  input  in_15,
  input  Input_2,
  input  Output_2,
  output out_18
);

  wire Clock_2_clock_status, Clock_2_value, Clock_out, Clock_Select_out, Halt_out, Register_2__0_2,
       Register_2__1_2, Register_2__2_2, Register_2__3_2, Register_2__4_2, Register_2__5_2, Register_2__6_2,
       Register_2__7_2, Register_3__0_2, Register_3__1_2, Register_3__2_2, Register_3__3_2, Register_3__4_2,
       Register_3__5_2, Register_3__6_2, Register_3__7_2, Register_4__0_2, Register_4__1_2, Register_4__2_2,
       Register_4__3_2, Register_4__4_2, Register_4__5_2, Register_4__6_2, Register_4__7_2, Register__0_2,
       Register__1_2, Register__2_2, Register__3_2, Register__4_2, Register__5_2, Register__6_2,
       Register__7_2, Step_out, Step_Select_out;
  wire [7:0] Register_3__8_bit_output, Register_4__8_bit_output, Register__8_bit_output;

  Clock_part Clock (.out(Clock_out));
  Button Clock_Select (.out(Clock_Select_out));
  Button Step_Select (.out(Step_Select_out));
  LED Clock_Status (.in(Clock_2_clock_status));
  Button Step (.out(Step_out));
  Button Halt (.out(Halt_out));
  _1_Bit_Register u_1_bit_register_1 ();  // open: CLK, Load, Data, Output
  Register Register (
    .CLK(Clock_2_value), .Load(Input), ._7(Register__8_bit_output[7]), ._6(Register__8_bit_output[6]),
    ._5(Register__8_bit_output[5]), ._4(Register__8_bit_output[4]), ._3(Register__8_bit_output[3]),
    ._2(Register__8_bit_output[2]), ._1(Register__8_bit_output[1]), ._0(Register__8_bit_output[0]),
    .Enable(Output), ._7_2(Register__7_2), ._6_2(Register__6_2), ._5_2(Register__5_2), ._4_2(Register__4_2),
    ._3_2(Register__3_2), ._2_2(Register__2_2), ._1_2(Register__1_2), ._0_2(Register__0_2),
    ._8_Bit_Output(Register__8_bit_output));
  DotMatrix #(.matrixcols(8), .matrixrows(1)) dotmatrix_1 (
    .col0(Register__7_2), .col1(Register__6_2), .col2(Register__5_2), .col3(Register__4_2),
    .col4(Register__3_2), .col5(Register__2_2), .col6(Register__1_2), .col7(Register__0_2));
  Register Register_2 (
    .CLK(Clock_2_value), .Load(Input_2), ._7(Register__8_bit_output[7]), ._6(Register__8_bit_output[6]),
    ._5(Register__8_bit_output[5]), ._4(Register__8_bit_output[4]), ._3(Register__8_bit_output[3]),
    ._2(Register__8_bit_output[2]), ._1(Register__8_bit_output[1]), ._0(Register__8_bit_output[0]),
    .Enable(Output_2), ._7_2(Register_2__7_2), ._6_2(Register_2__6_2), ._5_2(Register_2__5_2),
    ._4_2(Register_2__4_2), ._3_2(Register_2__3_2), ._2_2(Register_2__2_2), ._1_2(Register_2__1_2),
    ._0_2(Register_2__0_2), ._8_Bit_Output(Register__8_bit_output));
  DotMatrix #(.matrixcols(8), .matrixrows(1)) dotmatrix_2 (
    .col0(Register_2__7_2), .col1(Register_2__6_2), .col2(Register_2__5_2), .col3(Register_2__4_2),
    .col4(Register_2__3_2), .col5(Register_2__2_2), .col6(Register_2__1_2), .col7(Register_2__0_2));
  LED Throughput (.in(Clock_2_value));
  Clock Clock_2 (
    .Clock(Clock_out), .Clock_Select(Clock_Select_out), .Clock_Status(Clock_2_clock_status),
    .Step_Select(Step_Select_out), .Halt(Halt_out), .Step(Step_out), .Value(Clock_2_value));
  assign Register__8_bit_output[7] = in_9 ? in_1 : 1'bz;  // Controlled_Buffer controlled_buffer_1
  assign Register__8_bit_output[6] = in_9 ? in_2 : 1'bz;  // Controlled_Buffer controlled_buffer_2
  Pull_Resistor pull_resistor_1 (.node(Register__8_bit_output[7]));
  Pull_Resistor pull_resistor_2 (.node(Register__8_bit_output[6]));
  assign Register__8_bit_output[5] = in_9 ? in_3 : 1'bz;  // Controlled_Buffer controlled_buffer_3
  assign Register__8_bit_output[3] = in_9 ? in_5 : 1'bz;  // Controlled_Buffer controlled_buffer_4
  assign Register__8_bit_output[4] = in_9 ? in_4 : 1'bz;  // Controlled_Buffer controlled_buffer_5
  assign Register__8_bit_output[2] = in_9 ? in_6 : 1'bz;  // Controlled_Buffer controlled_buffer_6
  Pull_Resistor pull_resistor_3 (.node(Register__8_bit_output[4]));
  Pull_Resistor pull_resistor_4 (.node(Register__8_bit_output[5]));
  Pull_Resistor pull_resistor_5 (.node(Register__8_bit_output[2]));
  Pull_Resistor pull_resistor_6 (.node(Register__8_bit_output[3]));
  assign Register__8_bit_output[1] = in_9 ? in_7 : 1'bz;  // Controlled_Buffer controlled_buffer_7
  assign Register__8_bit_output[0] = in_9 ? in_8 : 1'bz;  // Controlled_Buffer controlled_buffer_8
  Pull_Resistor pull_resistor_7 (.node(Register__8_bit_output[0]));
  Pull_Resistor pull_resistor_8 (.node(Register__8_bit_output[1]));
  Register Register_3 (
    .CLK(Clock_2_value), .Load(in_15), ._7(Register__8_bit_output[7]), ._6(Register__8_bit_output[6]),
    ._5(Register__8_bit_output[5]), ._4(Register__8_bit_output[4]), ._3(Register__8_bit_output[3]),
    ._2(Register__8_bit_output[2]), ._1(Register__8_bit_output[1]), ._0(Register__8_bit_output[0]),
    .Enable(1'b1), ._7_2(Register_3__7_2), ._6_2(Register_3__6_2), ._5_2(Register_3__5_2),
    ._4_2(Register_3__4_2), ._3_2(Register_3__3_2), ._2_2(Register_3__2_2), ._1_2(Register_3__1_2),
    ._0_2(Register_3__0_2), ._8_Bit_Output(Register_3__8_bit_output));
  DotMatrix #(.matrixcols(8), .matrixrows(1)) dotmatrix_3 (
    .col0(Register_3__7_2), .col1(Register_3__6_2), .col2(Register_3__5_2), .col3(Register_3__4_2),
    .col4(Register_3__3_2), .col5(Register_3__2_2), .col6(Register_3__1_2), .col7(Register_3__0_2));
  Register Register_4 (
    .CLK(Clock_2_value), .Load(in_12), ._7(Register__8_bit_output[7]), ._6(Register__8_bit_output[6]),
    ._5(Register__8_bit_output[5]), ._4(Register__8_bit_output[4]), ._3(Register__8_bit_output[3]),
    ._2(Register__8_bit_output[2]), ._1(Register__8_bit_output[1]), ._0(Register__8_bit_output[0]),
    .Enable(1'b1), ._7_2(Register_4__7_2), ._6_2(Register_4__6_2), ._5_2(Register_4__5_2),
    ._4_2(Register_4__4_2), ._3_2(Register_4__3_2), ._2_2(Register_4__2_2), ._1_2(Register_4__1_2),
    ._0_2(Register_4__0_2), ._8_Bit_Output(Register_4__8_bit_output));
  DotMatrix #(.matrixcols(8), .matrixrows(1)) dotmatrix_4 (
    .col0(Register_4__7_2), .col1(Register_4__6_2), .col2(Register_4__5_2), .col3(Register_4__4_2),
    .col4(Register_4__3_2), .col5(Register_4__2_2), .col6(Register_4__1_2), .col7(Register_4__0_2));
  ALU alu_1 (
    ._7(Register__8_bit_output[7]), ._6(Register__8_bit_output[6]), ._5(Register__8_bit_output[5]),
    ._4(Register__8_bit_output[4]), ._3(Register__8_bit_output[3]), ._2(Register__8_bit_output[2]),
    ._1(Register__8_bit_output[1]), ._0(Register__8_bit_output[0]), .Enable(Enable), .Subtract(Subtract),
    .A7(Register_4__8_bit_output[7]), .A6(Register_4__8_bit_output[6]), .A5(Register_4__8_bit_output[5]),
    .A4(Register_4__8_bit_output[4]), .A3(Register_4__8_bit_output[3]), .A2(Register_4__8_bit_output[2]),
    .A1(Register_4__8_bit_output[1]), .A0(Register_4__8_bit_output[0]), .B7(Register_3__8_bit_output[7]),
    .B6(Register_3__8_bit_output[6]), .B5(Register_3__8_bit_output[5]), .B4(Register_3__8_bit_output[4]),
    .B3(Register_3__8_bit_output[3]), .B2(Register_3__8_bit_output[2]), .B1(Register_3__8_bit_output[1]),
    .B0(Register_3__8_bit_output[0]));
endmodule

module Clock (
  input  Clock,
  input  Clock_Select,
  input  Step_Select,
  input  Halt,
  input  Step,
  output Clock_Status,
  output Value
);

  wire and_1_out, and_2_out, not_2_out, or_1_out, Switch_q;

  Switch Switch (.in_1(Clock_Select), .in_2(or_1_out), .Q(Switch_q));
  or or_1 (or_1_out, Step_Select, Halt);
  not not_1 (Clock_Status, Switch_q);
  and and_1 (and_1_out, Clock, Clock_Status);
  and and_2 (and_2_out, Step, not_2_out);
  not not_2 (not_2_out, Clock_Status);
  or or_2 (Value, and_1_out, and_2_out);

  // Notes on the sheet:
  //   1 = ON, 0 = OFF
  //   When Step is triggered, it will
  //   advance the clock 1 tick
endmodule

module Switch_2 (
  input  Switch_Toggle,
  output Switch_Value
);

  wire button_1_out, d_ff_1_qn;

  Button button_1 (.out(button_1_out));
  D_Flip_Flop_part d_ff_1 (
    .clk(button_1_out), .D(d_ff_1_qn), .Q(Switch_Value), .Qn(d_ff_1_qn));  // open: preset, en, reset
endmodule

module D_Flip_Flop (
  input  CLK,
  input  D,
  output Q,
  output nQ
);

  wire and_1_out, and_2_out, not_1_out;

  not not_1 (not_1_out, D);
  and and_1 (and_1_out, not_1_out, CLK);
  and and_2 (and_2_out, CLK, D);
  nor nor_1 (Q, and_1_out, nQ);
  nor nor_2 (nQ, Q, and_2_out);
endmodule

module SR_Latch (
  input  in_1,
  input  in_2,
  output Q,
  output nQ
);

  nor nor_1 (Q, in_1, nQ);
  nor nor_2 (nQ, Q, in_2);
endmodule

module Switch (
  input  in_1,
  input  in_2,
  output Q
);

  SR_Latch SR_Latch (.in_1(in_1), .in_2(in_2), .Q(Q));  // open: nQ
endmodule

module Register (
  input  CLK,
  input  Load,
  input  _7,
  input  _6,
  input  _5,
  input  _4,
  input  _3,
  input  _2,
  input  _1,
  input  _0,
  input  Enable,
  output _7_2,
  output _6_2,
  output _5_2,
  output _4_2,
  output _3_2,
  output _2_2,
  output _1_2,
  output _0_2,
  output [7:0] _8_Bit_Output
);

  _1_Bit_Register Bit_0 (.CLK(CLK), .Load(Load), .Data(_0), .Output(_0_2));
  _1_Bit_Register Bit_1 (.CLK(CLK), .Load(Load), .Data(_1), .Output(_1_2));
  _1_Bit_Register Bit_2 (.CLK(CLK), .Load(Load), .Data(_2), .Output(_2_2));
  _1_Bit_Register Bit_3 (.CLK(CLK), .Load(Load), .Data(_3), .Output(_3_2));
  _1_Bit_Register Bit_4 (.CLK(CLK), .Load(Load), .Data(_4), .Output(_4_2));
  _1_Bit_Register Bit_5 (.CLK(CLK), .Load(Load), .Data(_5), .Output(_5_2));
  _1_Bit_Register Bit_6 (.CLK(CLK), .Load(Load), .Data(_6), .Output(_6_2));
  _1_Bit_Register Bit_7 (.CLK(CLK), .Load(Load), .Data(_7), .Output(_7_2));
  assign _8_Bit_Output = Enable ? {_7_2, _6_2, _5_2, _4_2, _3_2, _2_2, _1_2, _0_2} : 8'bz;  // Controlled_Buffer controlled_buffer_1
endmodule

module _1_Bit_Register (
  input  CLK,
  input  Load,
  input  Data,
  output Output
);

  wire and_1_out, and_2_out, controlled_buffer_1_out, not_1_out, or_1_out;

  assign controlled_buffer_1_out = Load ? Data : 1'bz;  // Controlled_Buffer controlled_buffer_1
  not not_1 (not_1_out, Load);
  and and_1 (and_1_out, Load, controlled_buffer_1_out);
  or or_1 (or_1_out, and_1_out, and_2_out);
  and and_2 (and_2_out, not_1_out, Output);
  D_Flip_Flop_part d_ff_1 (.clk(CLK), .D(or_1_out), .Q(Output));  // open: Qn, preset, en, reset
endmodule

module _1_Bit_Adder (
  input  Carry_In,
  input  A,
  input  B,
  output Sum,
  output Carry_Out
);

  wire and_1_out, and_2_out, and_3_out, and_4_out, and_5_out, and_6_out, and_7_out, and_8_out, not_1_out,
       not_2_out, not_3_out, not_4_out, not_5_out, not_6_out, not_7_out, not_8_out, not_9_out;

  not not_1 (not_1_out, A);
  not not_2 (not_2_out, B);
  not not_3 (not_3_out, A);
  not not_4 (not_4_out, Carry_In);
  not not_5 (not_5_out, B);
  not not_6 (not_6_out, Carry_In);
  not not_7 (not_7_out, A);
  not not_8 (not_8_out, B);
  not not_9 (not_9_out, Carry_In);
  and and_1 (and_1_out, not_1_out, not_2_out, Carry_In);
  and and_2 (and_2_out, not_3_out, B, not_4_out);
  and and_3 (and_3_out, A, not_5_out, not_6_out);
  and and_4 (and_4_out, A, B, Carry_In);
  and and_5 (and_5_out, not_7_out, B, Carry_In);
  and and_6 (and_6_out, A, not_8_out, Carry_In);
  and and_7 (and_7_out, A, B, not_9_out);
  and and_8 (and_8_out, A, B, Carry_In);
  or or_1 (Sum, and_1_out, and_2_out, and_3_out, and_4_out);
  or or_2 (Carry_Out, and_5_out, and_6_out, and_7_out, and_8_out);
  // OR_Gate or_3 is placed but not wired
endmodule

module Adder (
  input  B7,
  input  B7_2,
  input  B6,
  input  B6_2,
  input  A5,
  input  B5,
  input  A4,
  input  B4,
  input  A3,
  input  B3,
  input  A2,
  input  B2,
  input  A1,
  input  B1,
  input  A0,
  input  B0,
  output _7,
  output _6,
  output _5,
  output _4,
  output _3,
  output _2,
  output _1,
  output _0
);

  wire n1_bit_adder_2_carry_out, n1_bit_adder_3_carry_out, n1_bit_adder_4_carry_out,
       n1_bit_adder_5_carry_out, n1_bit_adder_6_carry_out, n1_bit_adder_7_carry_out, n1_bit_adder_8_carry_out;

  _1_Bit_Adder u_1_bit_adder_1 (.A(B7), .B(B7_2), .Sum(_7), .Carry_In(n1_bit_adder_2_carry_out));  // open: Carry_Out
  _1_Bit_Adder u_1_bit_adder_2 (
    .Carry_Out(n1_bit_adder_2_carry_out), .A(B6), .B(B6_2), .Sum(_6), .Carry_In(n1_bit_adder_3_carry_out));
  _1_Bit_Adder u_1_bit_adder_3 (
    .Carry_Out(n1_bit_adder_3_carry_out), .A(A5), .B(B5), .Sum(_5), .Carry_In(n1_bit_adder_4_carry_out));
  _1_Bit_Adder u_1_bit_adder_4 (
    .Carry_Out(n1_bit_adder_4_carry_out), .A(A4), .B(B4), .Sum(_4), .Carry_In(n1_bit_adder_6_carry_out));
  _1_Bit_Adder u_1_bit_adder_5 (
    .Carry_Out(n1_bit_adder_5_carry_out), .A(A2), .B(B2), .Sum(_2), .Carry_In(n1_bit_adder_8_carry_out));
  _1_Bit_Adder u_1_bit_adder_6 (
    .Carry_Out(n1_bit_adder_6_carry_out), .A(A3), .B(B3), .Sum(_3), .Carry_In(n1_bit_adder_5_carry_out));
  _1_Bit_Adder u_1_bit_adder_7 (.Carry_Out(n1_bit_adder_7_carry_out), .A(A0), .B(B0), .Sum(_0), .Carry_In(1'b0));
  _1_Bit_Adder u_1_bit_adder_8 (
    .Carry_Out(n1_bit_adder_8_carry_out), .A(A1), .B(B1), .Sum(_1), .Carry_In(n1_bit_adder_7_carry_out));
endmodule

module ALU (
  input  A7,
  input  A6,
  input  A5,
  input  A4,
  input  A3,
  input  A2,
  input  A1,
  input  A0,
  input  Enable,
  input  Subtract,
  input  B7,
  input  B6,
  input  B5,
  input  B4,
  input  B3,
  input  B2,
  input  B1,
  input  B0,
  output _7,
  output _6,
  output _5,
  output _4,
  output _3,
  output _2,
  output _1,
  output _0
);

  wire adder2_1__0, adder2_1__1, adder2_1__2, adder2_1__3, adder2_1__4, adder2_1__5, adder2_1__6,
       adder2_1__7, xor_1_out, xor_2_out, xor_3_out, xor_4_out, xor_5_out, xor_6_out, xor_7_out, xor_8_out;

  assign _7 = Enable ? adder2_1__7 : 1'bz;  // Controlled_Buffer controlled_buffer_1
  assign _6 = Enable ? adder2_1__6 : 1'bz;  // Controlled_Buffer controlled_buffer_2
  assign _5 = Enable ? adder2_1__5 : 1'bz;  // Controlled_Buffer controlled_buffer_3
  assign _4 = Enable ? adder2_1__4 : 1'bz;  // Controlled_Buffer controlled_buffer_4
  assign _3 = Enable ? adder2_1__3 : 1'bz;  // Controlled_Buffer controlled_buffer_5
  assign _2 = Enable ? adder2_1__2 : 1'bz;  // Controlled_Buffer controlled_buffer_6
  assign _1 = Enable ? adder2_1__1 : 1'bz;  // Controlled_Buffer controlled_buffer_7
  assign _0 = Enable ? adder2_1__0 : 1'bz;  // Controlled_Buffer controlled_buffer_8
  xor xor_1 (xor_1_out, B7, Subtract);
  Adder2 adder2_1 (
    ._7(adder2_1__7), ._6(adder2_1__6), ._5(adder2_1__5), ._4(adder2_1__4), ._3(adder2_1__3),
    ._2(adder2_1__2), ._1(adder2_1__1), ._0(adder2_1__0), .A7(A7), .A6(A6), .A5(A5), .A4(A4), .A3(A3),
    .A2(A2), .A1(A1), .A0(A0), .B7(xor_1_out), .B6(xor_3_out), .B5(xor_2_out), .B4(xor_5_out),
    .B3(xor_4_out), .B2(xor_6_out), .B1(xor_7_out), .B0(xor_8_out), .Carry_In(Subtract));
  xor xor_2 (xor_2_out, B5, Subtract);
  xor xor_3 (xor_3_out, B6, Subtract);
  xor xor_4 (xor_4_out, B3, Subtract);
  xor xor_5 (xor_5_out, B4, Subtract);
  xor xor_6 (xor_6_out, B2, Subtract);
  xor xor_7 (xor_7_out, B1, Subtract);
  xor xor_8 (xor_8_out, B0, Subtract);
endmodule

module Adder2 (
  input  A7,
  input  A6,
  input  A5,
  input  A4,
  input  A3,
  input  A2,
  input  A1,
  input  A0,
  input  Carry_In,
  input  B7,
  input  B6,
  input  B5,
  input  B4,
  input  B3,
  input  B2,
  input  B1,
  input  B0,
  output _7,
  output _6,
  output _5,
  output _4,
  output _3,
  output _2,
  output _1,
  output _0
);

  wire n1_bit_adder_2_2_carry_out, n1_bit_adder_2_3_carry_out, n1_bit_adder_2_4_carry_out,
       n1_bit_adder_2_5_carry_out, n1_bit_adder_2_6_carry_out, n1_bit_adder_2_7_carry_out,
       n1_bit_adder_2_8_carry_out;

  _1_Bit_Adder_2 u_1_bit_adder_2_1 (
    .Sum(_7), .A(A7), .B(B7), .Carry_In(n1_bit_adder_2_2_carry_out));  // open: Carry_Out
  _1_Bit_Adder_2 u_1_bit_adder_2_2 (
    .Carry_Out(n1_bit_adder_2_2_carry_out), .Sum(_6), .A(A6), .B(B6), .Carry_In(n1_bit_adder_2_4_carry_out));
  _1_Bit_Adder_2 u_1_bit_adder_2_3 (
    .Carry_Out(n1_bit_adder_2_3_carry_out), .Sum(_4), .A(A4), .B(B4), .Carry_In(n1_bit_adder_2_5_carry_out));
  _1_Bit_Adder_2 u_1_bit_adder_2_4 (
    .Carry_Out(n1_bit_adder_2_4_carry_out), .Sum(_5), .A(A5), .B(B5), .Carry_In(n1_bit_adder_2_3_carry_out));
  _1_Bit_Adder_2 u_1_bit_adder_2_5 (
    .Carry_Out(n1_bit_adder_2_5_carry_out), .Sum(_3), .A(A3), .B(B3), .Carry_In(n1_bit_adder_2_7_carry_out));
  _1_Bit_Adder_2 u_1_bit_adder_2_6 (
    .Carry_Out(n1_bit_adder_2_6_carry_out), .Sum(_1), .A(A1), .B(B1), .Carry_In(n1_bit_adder_2_8_carry_out));
  _1_Bit_Adder_2 u_1_bit_adder_2_7 (
    .Carry_Out(n1_bit_adder_2_7_carry_out), .Sum(_2), .A(A2), .B(B2), .Carry_In(n1_bit_adder_2_6_carry_out));
  _1_Bit_Adder_2 u_1_bit_adder_2_8 (
    .Carry_Out(n1_bit_adder_2_8_carry_out), .Sum(_0), .A(A0), .B(B0), .Carry_In(Carry_In));
endmodule

module _1_Bit_Adder_2 (
  input  Carry_In,
  input  A,
  input  B,
  output Carry_Out,
  output Sum
);

  wire and_1_out, and_2_out, and_3_out, and_4_out, and_5_out, and_6_out, and_7_out, and_8_out, not_1_out,
       not_2_out, not_3_out, not_4_out, not_5_out, not_6_out, not_7_out, not_8_out, not_9_out;

  not not_1 (not_1_out, A);
  and and_1 (and_1_out, not_1_out, not_2_out, Carry_In);
  not not_2 (not_2_out, B);
  not not_3 (not_3_out, A);
  and and_2 (and_2_out, not_3_out, B, not_4_out);
  not not_4 (not_4_out, Carry_In);
  not not_5 (not_5_out, B);
  and and_3 (and_3_out, A, not_5_out, not_6_out);
  not not_6 (not_6_out, Carry_In);
  and and_4 (and_4_out, A, B, Carry_In);
  not not_7 (not_7_out, A);
  and and_5 (and_5_out, not_7_out, B, Carry_In);
  and and_6 (and_6_out, A, not_8_out, Carry_In);
  not not_8 (not_8_out, B);
  and and_7 (and_7_out, A, B, not_9_out);
  not not_9 (not_9_out, Carry_In);
  and and_8 (and_8_out, A, B, Carry_In);
  or or_1 (Sum, and_1_out, and_2_out, and_3_out, and_4_out);
  or or_2 (Carry_Out, and_5_out, and_6_out, and_7_out, and_8_out);
  // OR_Gate or_3 is placed but not wired
endmodule
